// Logisim project 32_bit_cpu.circ as structural Verilog: 10 circuits, main circuit main
module main (
  input  [31:0] PERIPH_BUS_IN,
  output [21:0] PERIPH_BUS_OUT
);

  wire CU_acc_write_enable, CU_aux_write_enable, CU_flag_write_enable, CU_g1_write_enable,
       CU_g2_write_enable, CU_g3_write_enable, CU_g4_write_enable, CU_pc_write_enable, or_1_out, or_4_out,
       or_5_out, or_7_out, or_8_out, or_9_out;
  wire [1:0] CU_mem_addr_out;
  wire [2:0] or_3_out;
  wire [21:0] CU_mem_addr_out_2, demultiplexer_2_out1, demultiplexer_2_out2, demultiplexer_2_out3;
  wire [31:0] ACC_q, AUX_q, demultiplexer_1_out0, demultiplexer_1_out1, demultiplexer_1_out2,
       demultiplexer_1_out3, demultiplexer_1_out4, demultiplexer_1_out5, demultiplexer_1_out6,
       demultiplexer_1_out7, FLAG_q, GLP1_q, GLP2_q, GLP3_q, GLP4_q, PC_q, ram_1_dout, ram_2_dout,
       register_1_q, rom_1_data, undriven;

  or or_1 (or_1_out, CU_g1_write_enable, CU_g3_write_enable);
  or or_2 (or_3_out[1], or_5_out, or_7_out);
  or or_3 (or_3_out[0], or_1_out, or_4_out);
  or or_4 (or_4_out, CU_acc_write_enable, CU_pc_write_enable);
  or or_5 (or_5_out, CU_g2_write_enable, CU_g3_write_enable);
  Register #(.width(32)) GLP1 (.D(demultiplexer_1_out0), .en(CU_g1_write_enable), .Q(GLP1_q));  // open: clk, clr
  Register #(.width(32)) GLP2 (.D(demultiplexer_1_out1), .en(CU_g2_write_enable), .Q(GLP2_q));  // open: clk, clr
  Register #(.width(32)) GLP3 (.D(demultiplexer_1_out2), .en(CU_g3_write_enable), .Q(GLP3_q));  // open: clk, clr
  Register #(.width(32)) GLP4 (.D(demultiplexer_1_out3), .en(CU_g4_write_enable), .Q(GLP4_q));  // open: clk, clr
  or or_6 (or_3_out[2], or_8_out, or_9_out);
  or or_7 (or_7_out, CU_aux_write_enable, CU_pc_write_enable);
  or or_8 (or_8_out, CU_flag_write_enable, CU_acc_write_enable);
  or or_9 (or_9_out, CU_aux_write_enable, CU_pc_write_enable);
  Demultiplexer #(.select(3), .width(32)) demultiplexer_1 (
    .out0(demultiplexer_1_out0), .out1(demultiplexer_1_out1), .out2(demultiplexer_1_out2),
    .out3(demultiplexer_1_out3), .out4(demultiplexer_1_out4), .out5(demultiplexer_1_out5),
    .out6(demultiplexer_1_out6), .out7(demultiplexer_1_out7), .in(undriven), .sel(or_3_out));
  Register #(.width(32)) PC (.D(demultiplexer_1_out4), .en(CU_pc_write_enable), .Q(PC_q));  // open: clk, clr
  Register #(.width(32)) AUX (.D(demultiplexer_1_out5), .en(CU_aux_write_enable), .Q(AUX_q));  // open: clk, clr
  Register #(.width(32)) ACC (.D(demultiplexer_1_out6), .en(CU_acc_write_enable), .Q(ACC_q));  // open: clk, clr
  Register #(.width(32)) FLAG (.D(demultiplexer_1_out7), .en(CU_flag_write_enable), .Q(FLAG_q));  // open: clk, clr
  RAM #(.addrWidth(22), .dataWidth(32)) ram_1 (
    .addr(demultiplexer_2_out3), .dout(ram_1_dout));  // open: we, oe, clk, din
  Register #(.width(32)) register_1 (.Q(register_1_q));  // open: D, en, clk, clr
  ALU MAIN_ALU (
    .ACC(ACC_q), .CR_OUT(demultiplexer_1_out5), .ACC_OUT(demultiplexer_1_out6),
    .FLAGS_OUT(demultiplexer_1_out7));  // open: OPERAND_REG, OPCODE_SELECTOR
  Control_Unit CU (
    .IR_INPUT(register_1_q), .G4_IN(GLP4_q), .G3_IN(GLP3_q), .G2_IN(GLP2_q), .G1_IN(GLP1_q),
    .FLAG_IN(FLAG_q), .AUX_IN(AUX_q), .PC_IN(PC_q), .ACC_IN(ACC_q), .PC_WRITE_ENABLE(CU_pc_write_enable),
    .FLAG_WRITE_ENABLE(CU_flag_write_enable), .AUX_WRITE_ENABLE(CU_aux_write_enable),
    .ACC_WRITE_ENABLE(CU_acc_write_enable), .G4_WRITE_ENABLE(CU_g4_write_enable),
    .G3_WRITE_ENABLE(CU_g3_write_enable), .G2_WRITE_ENABLE(CU_g2_write_enable),
    .G1_WRITE_ENABLE(CU_g1_write_enable), .MEM_ADDR_OUT({CU_mem_addr_out, CU_mem_addr_out_2}));  // open: MEM_OUT, ACC_OUT, IR_OUT, FLAGS_OUT, G1_OUT, G2_OUT, G3_OUT, G4_OUT, PC_OUT, ALU_ENABLE, ALU_OP_OUT, ALU_OPERAND_OUT
  Multiplexer #(.select(2), .width(32)) multiplexer_1 (
    .in0(PERIPH_BUS_IN), .in1(rom_1_data), .in2(ram_2_dout), .in3(ram_1_dout), .sel(CU_mem_addr_out));  // open: out
  RAM #(.addrWidth(22), .dataWidth(32)) ram_2 (
    .addr(demultiplexer_2_out2), .dout(ram_2_dout));  // open: we, oe, clk, din
  Demultiplexer #(.select(2), .width(22)) demultiplexer_2 (
    .out0(PERIPH_BUS_OUT), .out1(demultiplexer_2_out1), .out2(demultiplexer_2_out2),
    .out3(demultiplexer_2_out3), .in(CU_mem_addr_out_2), .sel(CU_mem_addr_out));
  ROM #(.addrWidth(22), .dataWidth(32)) rom_1 (.addr(demultiplexer_2_out1), .data(rom_1_data));

  // Notes on the sheet:
  //   Program Counter
endmodule

module L_1_bit_half_adder_0ae93a57 (
  input  _0,
  input  _1,
  output Sum,
  output Carry
);

  xor xor_1 (Sum, _0, _1);
  buf and_1 (Carry, _0);  // AND_Gate
endmodule

module OR_32 (
  input  [31:0] in_1,
  input  [31:0] in_2,
  output [31:0] out_3
);

  buf or_1 (out_3[0], in_2[0]);  // OR_Gate
  buf or_2 (out_3[1], in_2[1]);  // OR_Gate
  buf or_3 (out_3[2], in_2[2]);  // OR_Gate
  buf or_4 (out_3[3], in_2[3]);  // OR_Gate
  buf or_5 (out_3[4], in_2[4]);  // OR_Gate
  buf or_6 (out_3[5], in_2[5]);  // OR_Gate
  buf or_7 (out_3[6], in_2[6]);  // OR_Gate
  buf or_8 (out_3[7], in_2[7]);  // OR_Gate
  buf or_9 (out_3[8], in_2[8]);  // OR_Gate
  buf or_10 (out_3[9], in_2[9]);  // OR_Gate
  buf or_11 (out_3[10], in_2[10]);  // OR_Gate
  buf or_12 (out_3[11], in_2[11]);  // OR_Gate
  buf or_13 (out_3[12], in_2[12]);  // OR_Gate
  buf or_14 (out_3[13], in_2[13]);  // OR_Gate
  buf or_15 (out_3[14], in_2[14]);  // OR_Gate
  buf or_16 (out_3[15], in_2[15]);  // OR_Gate
  buf or_17 (out_3[16], in_2[16]);  // OR_Gate
  buf or_18 (out_3[17], in_2[17]);  // OR_Gate
  buf or_19 (out_3[18], in_2[18]);  // OR_Gate
  buf or_20 (out_3[19], in_1[19]);  // OR_Gate
  buf or_21 (out_3[20], in_2[20]);  // OR_Gate
  buf or_22 (out_3[21], in_2[21]);  // OR_Gate
  buf or_23 (out_3[22], in_2[22]);  // OR_Gate
  buf or_24 (out_3[23], in_2[23]);  // OR_Gate
  buf or_25 (out_3[24], in_2[24]);  // OR_Gate
  buf or_26 (out_3[25], in_2[25]);  // OR_Gate
  buf or_27 (out_3[26], in_2[26]);  // OR_Gate
  buf or_28 (out_3[27], in_2[27]);  // OR_Gate
  buf or_29 (out_3[28], in_2[28]);  // OR_Gate
  buf or_30 (out_3[29], in_2[29]);  // OR_Gate
  buf or_31 (out_3[30], in_2[30]);  // OR_Gate
  buf or_32 (out_3[31], in_2[31]);  // OR_Gate
endmodule

module AND_32 (
  input  [31:0] Input_bus_1,
  input  [31:0] Input_bus_2,
  output [31:0] ACC_OUT
);

  buf and_1 (ACC_OUT[0], Input_bus_2[0]);  // AND_Gate
  buf and_2 (ACC_OUT[1], Input_bus_2[1]);  // AND_Gate
  buf and_3 (ACC_OUT[2], Input_bus_2[2]);  // AND_Gate
  buf and_4 (ACC_OUT[3], Input_bus_2[3]);  // AND_Gate
  buf and_5 (ACC_OUT[4], Input_bus_2[4]);  // AND_Gate
  buf and_6 (ACC_OUT[5], Input_bus_2[5]);  // AND_Gate
  buf and_7 (ACC_OUT[6], Input_bus_2[6]);  // AND_Gate
  buf and_8 (ACC_OUT[7], Input_bus_2[7]);  // AND_Gate
  buf and_9 (ACC_OUT[8], Input_bus_2[8]);  // AND_Gate
  buf and_10 (ACC_OUT[9], Input_bus_2[9]);  // AND_Gate
  buf and_11 (ACC_OUT[10], Input_bus_2[10]);  // AND_Gate
  buf and_12 (ACC_OUT[11], Input_bus_2[11]);  // AND_Gate
  buf and_13 (ACC_OUT[12], Input_bus_2[12]);  // AND_Gate
  buf and_14 (ACC_OUT[13], Input_bus_2[13]);  // AND_Gate
  buf and_15 (ACC_OUT[14], Input_bus_2[14]);  // AND_Gate
  buf and_16 (ACC_OUT[15], Input_bus_2[15]);  // AND_Gate
  buf and_17 (ACC_OUT[16], Input_bus_2[16]);  // AND_Gate
  buf and_18 (ACC_OUT[17], Input_bus_2[17]);  // AND_Gate
  buf and_19 (ACC_OUT[18], Input_bus_2[18]);  // AND_Gate
  buf and_20 (ACC_OUT[19], Input_bus_1[19]);  // AND_Gate
  buf and_21 (ACC_OUT[20], Input_bus_2[20]);  // AND_Gate
  buf and_22 (ACC_OUT[21], Input_bus_2[21]);  // AND_Gate
  buf and_23 (ACC_OUT[22], Input_bus_2[22]);  // AND_Gate
  buf and_24 (ACC_OUT[23], Input_bus_2[23]);  // AND_Gate
  buf and_25 (ACC_OUT[24], Input_bus_2[24]);  // AND_Gate
  buf and_26 (ACC_OUT[25], Input_bus_2[25]);  // AND_Gate
  buf and_27 (ACC_OUT[26], Input_bus_2[26]);  // AND_Gate
  buf and_28 (ACC_OUT[27], Input_bus_2[27]);  // AND_Gate
  buf and_29 (ACC_OUT[28], Input_bus_2[28]);  // AND_Gate
  buf and_30 (ACC_OUT[29], Input_bus_2[29]);  // AND_Gate
  buf and_31 (ACC_OUT[30], Input_bus_2[30]);  // AND_Gate
  buf and_32 (ACC_OUT[31], Input_bus_2[31]);  // AND_Gate
endmodule

module XOR_32 (
  input  [31:0] in_1,
  input  [31:0] in_2,
  output [31:0] out_3
);

  wire and_1_out, and_2_out, and_3_out, and_4_out, and_5_out, and_6_out, and_7_out, and_8_out, and_9_out,
       and_10_out, and_11_out, and_12_out, and_13_out, and_14_out, and_15_out, and_16_out, and_17_out,
       and_18_out, and_19_out, and_20_out, and_21_out, and_22_out, and_23_out, and_24_out, and_25_out,
       and_26_out, and_27_out, and_28_out, and_29_out, and_30_out, and_31_out, and_32_out, nor_1_out,
       nor_2_out, nor_3_out, nor_4_out, nor_5_out, nor_6_out, nor_7_out, nor_8_out, nor_9_out, nor_10_out,
       nor_11_out, nor_12_out, nor_13_out, nor_14_out, nor_15_out, nor_16_out, nor_17_out, nor_18_out,
       nor_19_out, nor_20_out, nor_21_out, nor_22_out, nor_23_out, nor_24_out, nor_25_out, nor_26_out,
       nor_27_out, nor_28_out, nor_29_out, nor_30_out, nor_31_out, nor_32_out;

  not nor_1 (nor_1_out, in_2[0]);  // NOR_Gate
  not nor_2 (nor_2_out, in_2[1]);  // NOR_Gate
  not nor_3 (nor_3_out, in_2[2]);  // NOR_Gate
  not nor_4 (nor_4_out, in_2[3]);  // NOR_Gate
  not nor_5 (nor_5_out, in_2[4]);  // NOR_Gate
  not nor_6 (nor_6_out, in_2[5]);  // NOR_Gate
  not nor_7 (nor_7_out, in_2[6]);  // NOR_Gate
  not nor_8 (nor_8_out, in_2[7]);  // NOR_Gate
  not nor_9 (nor_9_out, in_2[8]);  // NOR_Gate
  not nor_10 (nor_10_out, in_2[9]);  // NOR_Gate
  not nor_11 (nor_11_out, in_2[10]);  // NOR_Gate
  not nor_12 (nor_12_out, in_2[11]);  // NOR_Gate
  not nor_13 (nor_13_out, in_2[12]);  // NOR_Gate
  not nor_14 (nor_14_out, in_2[13]);  // NOR_Gate
  not nor_15 (nor_15_out, in_2[14]);  // NOR_Gate
  not nor_16 (nor_16_out, in_2[15]);  // NOR_Gate
  not nor_17 (nor_17_out, in_2[16]);  // NOR_Gate
  not nor_18 (nor_18_out, in_2[17]);  // NOR_Gate
  not nor_19 (nor_19_out, in_2[18]);  // NOR_Gate
  not nor_20 (nor_20_out, in_2[19]);  // NOR_Gate
  not nor_21 (nor_21_out, in_2[20]);  // NOR_Gate
  not nor_22 (nor_22_out, in_2[21]);  // NOR_Gate
  not nor_23 (nor_23_out, in_2[22]);  // NOR_Gate
  not nor_24 (nor_24_out, in_2[23]);  // NOR_Gate
  not nor_25 (nor_25_out, in_2[24]);  // NOR_Gate
  not nor_26 (nor_26_out, in_2[25]);  // NOR_Gate
  not nor_27 (nor_27_out, in_2[26]);  // NOR_Gate
  not nor_28 (nor_28_out, in_2[27]);  // NOR_Gate
  not nor_29 (nor_29_out, in_2[28]);  // NOR_Gate
  not nor_30 (nor_30_out, in_2[29]);  // NOR_Gate
  not nor_31 (nor_31_out, in_2[30]);  // NOR_Gate
  not nor_32 (nor_32_out, in_2[31]);  // NOR_Gate
  nor nor_33 (out_3[0], nor_1_out, and_1_out);
  // AND_Gate and_1 has open pins: out=and_1_out
  nor nor_34 (out_3[1], nor_2_out, and_2_out);
  // AND_Gate and_2 has open pins: out=and_2_out
  nor nor_35 (out_3[2], nor_3_out, and_3_out);
  // AND_Gate and_3 has open pins: out=and_3_out
  nor nor_36 (out_3[3], nor_4_out, and_4_out);
  // AND_Gate and_4 has open pins: out=and_4_out
  nor nor_37 (out_3[4], nor_5_out, and_5_out);
  // AND_Gate and_5 has open pins: out=and_5_out
  nor nor_38 (out_3[5], nor_6_out, and_6_out);
  // AND_Gate and_6 has open pins: out=and_6_out
  nor nor_39 (out_3[6], nor_7_out, and_7_out);
  // AND_Gate and_7 has open pins: out=and_7_out
  nor nor_40 (out_3[7], nor_8_out, and_8_out);
  // AND_Gate and_8 has open pins: out=and_8_out
  nor nor_41 (out_3[8], nor_9_out, and_9_out);
  // AND_Gate and_9 has open pins: out=and_9_out
  nor nor_42 (out_3[9], nor_10_out, and_10_out);
  // AND_Gate and_10 has open pins: out=and_10_out
  nor nor_43 (out_3[10], nor_11_out, and_11_out);
  // AND_Gate and_11 has open pins: out=and_11_out
  nor nor_44 (out_3[11], nor_12_out, and_12_out);
  // AND_Gate and_12 has open pins: out=and_12_out
  nor nor_45 (out_3[12], nor_13_out, and_13_out);
  // AND_Gate and_13 has open pins: out=and_13_out
  nor nor_46 (out_3[13], nor_14_out, and_14_out);
  // AND_Gate and_14 has open pins: out=and_14_out
  nor nor_47 (out_3[14], nor_15_out, and_15_out);
  // AND_Gate and_15 has open pins: out=and_15_out
  nor nor_48 (out_3[15], nor_16_out, and_16_out);
  // AND_Gate and_16 has open pins: out=and_16_out
  nor nor_49 (out_3[16], nor_17_out, and_17_out);
  // AND_Gate and_17 has open pins: out=and_17_out
  nor nor_50 (out_3[17], nor_18_out, and_18_out);
  // AND_Gate and_18 has open pins: out=and_18_out
  nor nor_51 (out_3[18], nor_19_out, and_19_out);
  // AND_Gate and_19 has open pins: out=and_19_out
  nor nor_52 (out_3[19], nor_20_out, and_20_out);
  // AND_Gate and_20 has open pins: out=and_20_out
  nor nor_53 (out_3[20], nor_21_out, and_21_out);
  // AND_Gate and_21 has open pins: out=and_21_out
  nor nor_54 (out_3[21], nor_22_out, and_22_out);
  // AND_Gate and_22 has open pins: out=and_22_out
  nor nor_55 (out_3[22], nor_23_out, and_23_out);
  // AND_Gate and_23 has open pins: out=and_23_out
  nor nor_56 (out_3[23], nor_24_out, and_24_out);
  // AND_Gate and_24 has open pins: out=and_24_out
  nor nor_57 (out_3[24], nor_25_out, and_25_out);
  // AND_Gate and_25 has open pins: out=and_25_out
  nor nor_58 (out_3[25], nor_26_out, and_26_out);
  // AND_Gate and_26 has open pins: out=and_26_out
  nor nor_59 (out_3[26], nor_27_out, and_27_out);
  // AND_Gate and_27 has open pins: out=and_27_out
  nor nor_60 (out_3[27], nor_28_out, and_28_out);
  // AND_Gate and_28 has open pins: out=and_28_out
  nor nor_61 (out_3[28], nor_29_out, and_29_out);
  // AND_Gate and_29 has open pins: out=and_29_out
  nor nor_62 (out_3[29], nor_30_out, and_30_out);
  // AND_Gate and_30 has open pins: out=and_30_out
  nor nor_63 (out_3[30], nor_31_out, and_31_out);
  // AND_Gate and_31 has open pins: out=and_31_out
  nor nor_64 (out_3[31], nor_32_out, and_32_out);
  // AND_Gate and_32 has open pins: out=and_32_out
endmodule

module L_1_bit_full_adder_dd117225 (
  input  Input_1,
  input  Input_2,
  input  Carry_In,
  output Output_1,
  output Carry_out
);

  wire and_1_out, and_2_out, xor_1_out;

  xor xor_1 (xor_1_out, Input_1, Input_2);
  xor xor_2 (Output_1, xor_1_out, Carry_In);
  and and_1 (and_1_out, xor_1_out, Carry_In);
  and and_2 (and_2_out, Input_1, Input_2);
  or or_1 (Carry_out, and_1_out, and_2_out);

  // Notes on the sheet:
  //   Sum
  //   Carry
endmodule

module ADD_32 (
  input  [31:0] Input_bus_1,
  input  [31:0] Input_bus_2,
  input  Control_Pin_72d4b5d9,
  output [31:0] Output_bus_1,
  output Output_1
);

  wire L_1_bit_full_adder_dd117225_1_carry_out, L_1_bit_full_adder_dd117225_2_carry_out,
       L_1_bit_full_adder_dd117225_3_carry_out, L_1_bit_full_adder_dd117225_4_carry_out,
       L_1_bit_full_adder_dd117225_5_carry_out, L_1_bit_full_adder_dd117225_6_carry_out,
       L_1_bit_full_adder_dd117225_7_carry_out, L_1_bit_full_adder_dd117225_8_carry_out,
       L_1_bit_full_adder_dd117225_9_carry_out, L_1_bit_full_adder_dd117225_10_carry_out,
       L_1_bit_full_adder_dd117225_11_carry_out, L_1_bit_full_adder_dd117225_12_carry_out,
       L_1_bit_full_adder_dd117225_13_carry_out, L_1_bit_full_adder_dd117225_14_carry_out,
       L_1_bit_full_adder_dd117225_15_carry_out, L_1_bit_full_adder_dd117225_16_carry_out,
       L_1_bit_full_adder_dd117225_17_carry_out, L_1_bit_full_adder_dd117225_18_carry_out,
       L_1_bit_full_adder_dd117225_19_carry_out, L_1_bit_full_adder_dd117225_20_carry_out,
       L_1_bit_full_adder_dd117225_21_carry_out, L_1_bit_full_adder_dd117225_22_carry_out,
       L_1_bit_full_adder_dd117225_23_carry_out, L_1_bit_full_adder_dd117225_24_carry_out,
       L_1_bit_full_adder_dd117225_25_carry_out, L_1_bit_full_adder_dd117225_26_carry_out,
       L_1_bit_full_adder_dd117225_27_carry_out, L_1_bit_full_adder_dd117225_28_carry_out,
       L_1_bit_full_adder_dd117225_29_carry_out, L_1_bit_full_adder_dd117225_30_carry_out,
       L_1_bit_full_adder_dd117225_31_carry_out, multiplexer_1_out, multiplexer_2_out, multiplexer_3_out,
       multiplexer_4_out, multiplexer_5_out, multiplexer_6_out, multiplexer_7_out, multiplexer_8_out,
       multiplexer_9_out, multiplexer_10_out, multiplexer_11_out, multiplexer_12_out, multiplexer_13_out,
       multiplexer_14_out, multiplexer_15_out, multiplexer_16_out, multiplexer_17_out, multiplexer_18_out,
       multiplexer_19_out, multiplexer_20_out, multiplexer_21_out, multiplexer_22_out, multiplexer_23_out,
       multiplexer_24_out, multiplexer_25_out, multiplexer_26_out, multiplexer_27_out, multiplexer_28_out,
       multiplexer_29_out, multiplexer_30_out, multiplexer_31_out, multiplexer_32_out, not_1_out, not_2_out,
       not_3_out, not_4_out, not_5_out, not_6_out, not_7_out, not_8_out, not_9_out, not_10_out, not_11_out,
       not_12_out, not_13_out, not_14_out, not_15_out, not_16_out, not_17_out, not_18_out, not_19_out,
       not_20_out, not_21_out, not_22_out, not_23_out, not_24_out, not_25_out, not_26_out, not_27_out,
       not_28_out, not_29_out, not_30_out, not_31_out, not_32_out;

  Multiplexer multiplexer_1 (
    .in0(Input_bus_2[0]), .in1(not_1_out), .out(multiplexer_1_out), .sel(Control_Pin_72d4b5d9));
  not not_1 (not_1_out, Input_bus_2[0]);
  Multiplexer multiplexer_2 (
    .in0(Input_bus_2[1]), .in1(not_2_out), .out(multiplexer_2_out), .sel(Control_Pin_72d4b5d9));
  not not_2 (not_2_out, Input_bus_2[1]);
  Multiplexer multiplexer_3 (
    .in0(Input_bus_2[2]), .in1(not_3_out), .out(multiplexer_3_out), .sel(Control_Pin_72d4b5d9));
  not not_3 (not_3_out, Input_bus_2[2]);
  Multiplexer multiplexer_4 (
    .in0(Input_bus_2[3]), .in1(not_4_out), .out(multiplexer_4_out), .sel(Control_Pin_72d4b5d9));
  not not_4 (not_4_out, Input_bus_2[3]);
  Multiplexer multiplexer_5 (
    .in0(Input_bus_2[4]), .in1(not_5_out), .out(multiplexer_5_out), .sel(Control_Pin_72d4b5d9));
  not not_5 (not_5_out, Input_bus_2[4]);
  Multiplexer multiplexer_6 (
    .in0(Input_bus_2[5]), .in1(not_6_out), .out(multiplexer_6_out), .sel(Control_Pin_72d4b5d9));
  not not_6 (not_6_out, Input_bus_2[5]);
  Multiplexer multiplexer_7 (
    .in0(Input_bus_2[6]), .in1(not_7_out), .out(multiplexer_7_out), .sel(Control_Pin_72d4b5d9));
  not not_7 (not_7_out, Input_bus_2[6]);
  Multiplexer multiplexer_8 (
    .in0(Input_bus_2[7]), .in1(not_8_out), .out(multiplexer_8_out), .sel(Control_Pin_72d4b5d9));
  not not_8 (not_8_out, Input_bus_2[7]);
  Multiplexer multiplexer_9 (
    .in0(Input_bus_2[8]), .in1(not_9_out), .out(multiplexer_9_out), .sel(Control_Pin_72d4b5d9));
  not not_9 (not_9_out, Input_bus_2[8]);
  Multiplexer multiplexer_10 (
    .in0(Input_bus_2[9]), .in1(not_10_out), .out(multiplexer_10_out), .sel(Control_Pin_72d4b5d9));
  not not_10 (not_10_out, Input_bus_2[9]);
  Multiplexer multiplexer_11 (
    .in0(Input_bus_2[10]), .in1(not_11_out), .out(multiplexer_11_out), .sel(Control_Pin_72d4b5d9));
  not not_11 (not_11_out, Input_bus_2[10]);
  Multiplexer multiplexer_12 (
    .in0(Input_bus_2[11]), .in1(not_12_out), .out(multiplexer_12_out), .sel(Control_Pin_72d4b5d9));
  not not_12 (not_12_out, Input_bus_2[11]);
  Multiplexer multiplexer_13 (
    .in0(Input_bus_2[12]), .in1(not_13_out), .out(multiplexer_13_out), .sel(Control_Pin_72d4b5d9));
  not not_13 (not_13_out, Input_bus_2[12]);
  Multiplexer multiplexer_14 (
    .in0(Input_bus_2[13]), .in1(not_14_out), .out(multiplexer_14_out), .sel(Control_Pin_72d4b5d9));
  not not_14 (not_14_out, Input_bus_2[13]);
  Multiplexer multiplexer_15 (
    .in0(Input_bus_2[14]), .in1(not_15_out), .out(multiplexer_15_out), .sel(Control_Pin_72d4b5d9));
  not not_15 (not_15_out, Input_bus_2[14]);
  Multiplexer multiplexer_16 (
    .in0(Input_bus_2[15]), .in1(not_16_out), .out(multiplexer_16_out), .sel(Control_Pin_72d4b5d9));
  not not_16 (not_16_out, Input_bus_2[15]);
  Multiplexer multiplexer_17 (
    .in0(Input_bus_2[16]), .in1(not_17_out), .out(multiplexer_17_out), .sel(Control_Pin_72d4b5d9));
  not not_17 (not_17_out, Input_bus_2[16]);
  Multiplexer multiplexer_18 (
    .in0(Input_bus_2[17]), .in1(not_18_out), .out(multiplexer_18_out), .sel(Control_Pin_72d4b5d9));
  not not_18 (not_18_out, Input_bus_2[17]);
  Multiplexer multiplexer_19 (
    .in0(Input_bus_2[18]), .in1(not_19_out), .out(multiplexer_19_out), .sel(Control_Pin_72d4b5d9));
  not not_19 (not_19_out, Input_bus_2[18]);
  Multiplexer multiplexer_20 (
    .in0(Input_bus_2[19]), .in1(not_20_out), .out(multiplexer_20_out), .sel(Control_Pin_72d4b5d9));
  not not_20 (not_20_out, Input_bus_2[19]);
  Multiplexer multiplexer_21 (
    .in0(Input_bus_2[20]), .in1(not_21_out), .out(multiplexer_21_out), .sel(Control_Pin_72d4b5d9));
  not not_21 (not_21_out, Input_bus_2[20]);
  Multiplexer multiplexer_22 (
    .in0(Input_bus_2[21]), .in1(not_22_out), .out(multiplexer_22_out), .sel(Control_Pin_72d4b5d9));
  not not_22 (not_22_out, Input_bus_2[21]);
  Multiplexer multiplexer_23 (
    .in0(Input_bus_2[22]), .in1(not_23_out), .out(multiplexer_23_out), .sel(Control_Pin_72d4b5d9));
  not not_23 (not_23_out, Input_bus_2[22]);
  Multiplexer multiplexer_24 (
    .in0(Input_bus_2[23]), .in1(not_24_out), .out(multiplexer_24_out), .sel(Control_Pin_72d4b5d9));
  not not_24 (not_24_out, Input_bus_2[23]);
  Multiplexer multiplexer_25 (
    .in0(Input_bus_2[24]), .in1(not_25_out), .out(multiplexer_25_out), .sel(Control_Pin_72d4b5d9));
  not not_25 (not_25_out, Input_bus_2[24]);
  Multiplexer multiplexer_26 (
    .in0(Input_bus_2[25]), .in1(not_26_out), .out(multiplexer_26_out), .sel(Control_Pin_72d4b5d9));
  not not_26 (not_26_out, Input_bus_2[25]);
  Multiplexer multiplexer_27 (
    .in0(Input_bus_2[26]), .in1(not_27_out), .out(multiplexer_27_out), .sel(Control_Pin_72d4b5d9));
  not not_27 (not_27_out, Input_bus_2[26]);
  Multiplexer multiplexer_28 (
    .in0(Input_bus_2[27]), .in1(not_28_out), .out(multiplexer_28_out), .sel(Control_Pin_72d4b5d9));
  not not_28 (not_28_out, Input_bus_2[27]);
  Multiplexer multiplexer_29 (
    .in0(Input_bus_2[28]), .in1(not_29_out), .out(multiplexer_29_out), .sel(Control_Pin_72d4b5d9));
  not not_29 (not_29_out, Input_bus_2[28]);
  Multiplexer multiplexer_30 (
    .in0(Input_bus_2[29]), .in1(not_30_out), .out(multiplexer_30_out), .sel(Control_Pin_72d4b5d9));
  not not_30 (not_30_out, Input_bus_2[29]);
  Multiplexer multiplexer_31 (
    .in0(Input_bus_2[30]), .in1(not_31_out), .out(multiplexer_31_out), .sel(Control_Pin_72d4b5d9));
  not not_31 (not_31_out, Input_bus_2[30]);
  Multiplexer multiplexer_32 (
    .in0(Input_bus_2[31]), .in1(not_32_out), .out(multiplexer_32_out), .sel(Control_Pin_72d4b5d9));
  not not_32 (not_32_out, Input_bus_2[31]);
  L_1_bit_full_adder_dd117225 L_1_bit_full_adder_dd117225_1 (
    .Input_1(Input_bus_1[0]), .Input_2(multiplexer_1_out), .Carry_In(Control_Pin_72d4b5d9),
    .Output_1(Output_bus_1[0]), .Carry_out(L_1_bit_full_adder_dd117225_1_carry_out));
  L_1_bit_full_adder_dd117225 L_1_bit_full_adder_dd117225_2 (
    .Input_1(Input_bus_1[1]), .Input_2(multiplexer_2_out),
    .Carry_In(L_1_bit_full_adder_dd117225_1_carry_out), .Output_1(Output_bus_1[1]),
    .Carry_out(L_1_bit_full_adder_dd117225_2_carry_out));
  L_1_bit_full_adder_dd117225 L_1_bit_full_adder_dd117225_3 (
    .Input_1(Input_bus_1[2]), .Input_2(multiplexer_3_out),
    .Carry_In(L_1_bit_full_adder_dd117225_2_carry_out), .Output_1(Output_bus_1[2]),
    .Carry_out(L_1_bit_full_adder_dd117225_3_carry_out));
  L_1_bit_full_adder_dd117225 L_1_bit_full_adder_dd117225_4 (
    .Input_1(Input_bus_1[3]), .Input_2(multiplexer_4_out),
    .Carry_In(L_1_bit_full_adder_dd117225_3_carry_out), .Output_1(Output_bus_1[3]),
    .Carry_out(L_1_bit_full_adder_dd117225_4_carry_out));
  L_1_bit_full_adder_dd117225 L_1_bit_full_adder_dd117225_5 (
    .Input_1(Input_bus_1[4]), .Input_2(multiplexer_5_out),
    .Carry_In(L_1_bit_full_adder_dd117225_4_carry_out), .Output_1(Output_bus_1[4]),
    .Carry_out(L_1_bit_full_adder_dd117225_5_carry_out));
  L_1_bit_full_adder_dd117225 L_1_bit_full_adder_dd117225_6 (
    .Input_1(Input_bus_1[5]), .Input_2(multiplexer_6_out),
    .Carry_In(L_1_bit_full_adder_dd117225_5_carry_out), .Output_1(Output_bus_1[5]),
    .Carry_out(L_1_bit_full_adder_dd117225_6_carry_out));
  L_1_bit_full_adder_dd117225 L_1_bit_full_adder_dd117225_7 (
    .Input_1(Input_bus_1[6]), .Input_2(multiplexer_7_out),
    .Carry_In(L_1_bit_full_adder_dd117225_6_carry_out), .Output_1(Output_bus_1[6]),
    .Carry_out(L_1_bit_full_adder_dd117225_7_carry_out));
  L_1_bit_full_adder_dd117225 L_1_bit_full_adder_dd117225_8 (
    .Input_1(Input_bus_1[7]), .Input_2(multiplexer_8_out),
    .Carry_In(L_1_bit_full_adder_dd117225_7_carry_out), .Output_1(Output_bus_1[7]),
    .Carry_out(L_1_bit_full_adder_dd117225_8_carry_out));
  L_1_bit_full_adder_dd117225 L_1_bit_full_adder_dd117225_9 (
    .Input_1(Input_bus_1[8]), .Input_2(multiplexer_9_out),
    .Carry_In(L_1_bit_full_adder_dd117225_8_carry_out), .Output_1(Output_bus_1[8]),
    .Carry_out(L_1_bit_full_adder_dd117225_9_carry_out));
  L_1_bit_full_adder_dd117225 L_1_bit_full_adder_dd117225_10 (
    .Input_1(Input_bus_1[9]), .Input_2(multiplexer_10_out),
    .Carry_In(L_1_bit_full_adder_dd117225_9_carry_out), .Output_1(Output_bus_1[9]),
    .Carry_out(L_1_bit_full_adder_dd117225_10_carry_out));
  L_1_bit_full_adder_dd117225 L_1_bit_full_adder_dd117225_11 (
    .Input_1(Input_bus_1[10]), .Input_2(multiplexer_11_out),
    .Carry_In(L_1_bit_full_adder_dd117225_10_carry_out), .Output_1(Output_bus_1[10]),
    .Carry_out(L_1_bit_full_adder_dd117225_11_carry_out));
  L_1_bit_full_adder_dd117225 L_1_bit_full_adder_dd117225_12 (
    .Input_1(Input_bus_1[11]), .Input_2(multiplexer_12_out),
    .Carry_In(L_1_bit_full_adder_dd117225_11_carry_out), .Output_1(Output_bus_1[11]),
    .Carry_out(L_1_bit_full_adder_dd117225_12_carry_out));
  L_1_bit_full_adder_dd117225 L_1_bit_full_adder_dd117225_13 (
    .Input_1(Input_bus_1[12]), .Input_2(multiplexer_13_out),
    .Carry_In(L_1_bit_full_adder_dd117225_12_carry_out), .Output_1(Output_bus_1[12]),
    .Carry_out(L_1_bit_full_adder_dd117225_13_carry_out));
  L_1_bit_full_adder_dd117225 L_1_bit_full_adder_dd117225_14 (
    .Input_1(Input_bus_1[13]), .Input_2(multiplexer_14_out),
    .Carry_In(L_1_bit_full_adder_dd117225_13_carry_out), .Output_1(Output_bus_1[13]),
    .Carry_out(L_1_bit_full_adder_dd117225_14_carry_out));
  L_1_bit_full_adder_dd117225 L_1_bit_full_adder_dd117225_15 (
    .Input_1(Input_bus_1[14]), .Input_2(multiplexer_15_out),
    .Carry_In(L_1_bit_full_adder_dd117225_14_carry_out), .Output_1(Output_bus_1[14]),
    .Carry_out(L_1_bit_full_adder_dd117225_15_carry_out));
  L_1_bit_full_adder_dd117225 L_1_bit_full_adder_dd117225_16 (
    .Input_1(Input_bus_1[15]), .Input_2(multiplexer_16_out),
    .Carry_In(L_1_bit_full_adder_dd117225_15_carry_out), .Output_1(Output_bus_1[15]),
    .Carry_out(L_1_bit_full_adder_dd117225_16_carry_out));
  L_1_bit_full_adder_dd117225 L_1_bit_full_adder_dd117225_17 (
    .Input_1(Input_bus_1[16]), .Input_2(multiplexer_17_out),
    .Carry_In(L_1_bit_full_adder_dd117225_16_carry_out), .Output_1(Output_bus_1[16]),
    .Carry_out(L_1_bit_full_adder_dd117225_17_carry_out));
  L_1_bit_full_adder_dd117225 L_1_bit_full_adder_dd117225_18 (
    .Input_1(Input_bus_1[17]), .Input_2(multiplexer_18_out),
    .Carry_In(L_1_bit_full_adder_dd117225_17_carry_out), .Output_1(Output_bus_1[17]),
    .Carry_out(L_1_bit_full_adder_dd117225_18_carry_out));
  L_1_bit_full_adder_dd117225 L_1_bit_full_adder_dd117225_19 (
    .Input_1(Input_bus_1[18]), .Input_2(multiplexer_19_out),
    .Carry_In(L_1_bit_full_adder_dd117225_18_carry_out), .Output_1(Output_bus_1[18]),
    .Carry_out(L_1_bit_full_adder_dd117225_19_carry_out));
  L_1_bit_full_adder_dd117225 L_1_bit_full_adder_dd117225_20 (
    .Input_1(Input_bus_1[19]), .Input_2(multiplexer_20_out),
    .Carry_In(L_1_bit_full_adder_dd117225_19_carry_out), .Output_1(Output_bus_1[19]),
    .Carry_out(L_1_bit_full_adder_dd117225_20_carry_out));
  L_1_bit_full_adder_dd117225 L_1_bit_full_adder_dd117225_21 (
    .Input_1(Input_bus_1[20]), .Input_2(multiplexer_21_out),
    .Carry_In(L_1_bit_full_adder_dd117225_20_carry_out), .Output_1(Output_bus_1[20]),
    .Carry_out(L_1_bit_full_adder_dd117225_21_carry_out));
  L_1_bit_full_adder_dd117225 L_1_bit_full_adder_dd117225_22 (
    .Input_1(Input_bus_1[21]), .Input_2(multiplexer_22_out),
    .Carry_In(L_1_bit_full_adder_dd117225_21_carry_out), .Output_1(Output_bus_1[21]),
    .Carry_out(L_1_bit_full_adder_dd117225_22_carry_out));
  L_1_bit_full_adder_dd117225 L_1_bit_full_adder_dd117225_23 (
    .Input_1(Input_bus_1[22]), .Input_2(multiplexer_23_out),
    .Carry_In(L_1_bit_full_adder_dd117225_22_carry_out), .Output_1(Output_bus_1[22]),
    .Carry_out(L_1_bit_full_adder_dd117225_23_carry_out));
  L_1_bit_full_adder_dd117225 L_1_bit_full_adder_dd117225_24 (
    .Input_1(Input_bus_1[23]), .Input_2(multiplexer_24_out),
    .Carry_In(L_1_bit_full_adder_dd117225_23_carry_out), .Output_1(Output_bus_1[23]),
    .Carry_out(L_1_bit_full_adder_dd117225_24_carry_out));
  L_1_bit_full_adder_dd117225 L_1_bit_full_adder_dd117225_25 (
    .Input_1(Input_bus_1[24]), .Input_2(multiplexer_25_out),
    .Carry_In(L_1_bit_full_adder_dd117225_24_carry_out), .Output_1(Output_bus_1[24]),
    .Carry_out(L_1_bit_full_adder_dd117225_25_carry_out));
  L_1_bit_full_adder_dd117225 L_1_bit_full_adder_dd117225_26 (
    .Input_1(Input_bus_1[25]), .Input_2(multiplexer_26_out),
    .Carry_In(L_1_bit_full_adder_dd117225_25_carry_out), .Output_1(Output_bus_1[25]),
    .Carry_out(L_1_bit_full_adder_dd117225_26_carry_out));
  L_1_bit_full_adder_dd117225 L_1_bit_full_adder_dd117225_27 (
    .Input_1(Input_bus_1[26]), .Input_2(multiplexer_27_out),
    .Carry_In(L_1_bit_full_adder_dd117225_26_carry_out), .Output_1(Output_bus_1[26]),
    .Carry_out(L_1_bit_full_adder_dd117225_27_carry_out));
  L_1_bit_full_adder_dd117225 L_1_bit_full_adder_dd117225_28 (
    .Input_1(Input_bus_1[27]), .Input_2(multiplexer_28_out),
    .Carry_In(L_1_bit_full_adder_dd117225_27_carry_out), .Output_1(Output_bus_1[27]),
    .Carry_out(L_1_bit_full_adder_dd117225_28_carry_out));
  L_1_bit_full_adder_dd117225 L_1_bit_full_adder_dd117225_29 (
    .Input_1(Input_bus_1[28]), .Input_2(multiplexer_29_out),
    .Carry_In(L_1_bit_full_adder_dd117225_28_carry_out), .Output_1(Output_bus_1[28]),
    .Carry_out(L_1_bit_full_adder_dd117225_29_carry_out));
  L_1_bit_full_adder_dd117225 L_1_bit_full_adder_dd117225_30 (
    .Input_1(Input_bus_1[29]), .Input_2(multiplexer_30_out),
    .Carry_In(L_1_bit_full_adder_dd117225_29_carry_out), .Output_1(Output_bus_1[29]),
    .Carry_out(L_1_bit_full_adder_dd117225_30_carry_out));
  L_1_bit_full_adder_dd117225 L_1_bit_full_adder_dd117225_31 (
    .Input_1(Input_bus_1[30]), .Input_2(multiplexer_31_out),
    .Carry_In(L_1_bit_full_adder_dd117225_30_carry_out), .Output_1(Output_bus_1[30]),
    .Carry_out(L_1_bit_full_adder_dd117225_31_carry_out));
  L_1_bit_full_adder_dd117225 L_1_bit_full_adder_dd117225_32 (
    .Input_1(Input_bus_1[31]), .Input_2(multiplexer_32_out),
    .Carry_In(L_1_bit_full_adder_dd117225_31_carry_out), .Output_1(Output_bus_1[31]), .Carry_out(Output_1));

  // Notes on the sheet:
  //   Carry
endmodule

module Control_Unit (
  input  [31:0] IR_INPUT,
  input  [31:0] G4_IN,
  input  [31:0] G3_IN,
  input  [31:0] G2_IN,
  input  [31:0] G1_IN,
  input  [31:0] FLAG_IN,
  input  [31:0] AUX_IN,
  input  [31:0] PC_IN,
  input  [31:0] ACC_IN,
  output [2:0] ALU_OP_OUT,
  output ALU_ENABLE,
  output PC_WRITE_ENABLE,
  output G4_WRITE_ENABLE,
  output G3_WRITE_ENABLE,
  output [31:0] ALU_OPERAND_OUT,
  output G2_WRITE_ENABLE,
  output G1_WRITE_ENABLE,
  output FLAG_WRITE_ENABLE,
  output AUX_WRITE_ENABLE,
  output ACC_WRITE_ENABLE,
  output [31:0] PC_OUT,
  output [23:0] MEM_ADDR_OUT,
  output [31:0] MEM_OUT,
  output [31:0] ACC_OUT,
  output [31:0] IR_OUT,
  output [31:0] FLAGS_OUT,
  output [31:0] G1_OUT,
  output [31:0] G2_OUT,
  output [31:0] G3_OUT,
  output [31:0] G4_OUT
);

  wire and_1_out, and_2_out, and_3_out, and_4_out, and_5_out, and_6_out, and_7_out, and_8_out, and_9_out,
       and_10_out, and_11_out, and_12_out, and_13_out, and_14_out, and_15_out, and_16_out, and_17_out,
       and_18_out, and_19_out, and_20_out, and_21_out, and_22_out, and_23_out, and_24_out, and_25_out,
       and_26_out, and_27_out, and_28_out, and_29_out, and_30_out, and_31_out, and_32_out, and_33_out,
       and_34_out, and_35_out, and_36_out, and_37_out, and_38_out, and_39_out, and_40_out, and_41_out,
       and_42_out, and_43_out, and_44_out, demultiplexer_2_out6, not_1_out, not_2_out, not_3_out, not_4_out,
       not_5_out, not_6_out, not_7_out, not_8_out, not_9_out, not_10_out, not_11_out, not_12_out, not_13_out,
       not_14_out, not_15_out, not_16_out, not_17_out, not_18_out, not_19_out, not_20_out, or_3_out,
       pull_resistor_12_node;
  wire [2:0] multiplexer_2_out, multiplexer_4_out, multiplexer_7_out, pull_resistor_11_node,
       pull_resistor_13_node, pull_resistor_14_node;
  wire [23:0] multiplexer_1_out, pull_resistor_1_node;
  wire [31:0] multiplexer_5_out, multiplexer_6_out;
  wire [31:24] pull_resistor_2_node;
  wire [31:31] pull_resistor_10_node;

  Pull_Resistor pull_resistor_1 (.node(pull_resistor_1_node));
  Multiplexer #(.width(24)) multiplexer_1 (
    .in0(IR_INPUT[31:8]), .in1(pull_resistor_1_node), .out(multiplexer_1_out), .sel(ALU_ENABLE));
  Pull_Resistor pull_resistor_2 (.node(pull_resistor_2_node[24]));
  Pull_Resistor pull_resistor_3 (.node(pull_resistor_2_node[25]));
  Pull_Resistor pull_resistor_4 (.node(pull_resistor_2_node[26]));
  Pull_Resistor pull_resistor_5 (.node(pull_resistor_2_node[27]));
  Pull_Resistor pull_resistor_6 (.node(pull_resistor_2_node[28]));
  Pull_Resistor pull_resistor_7 (.node(pull_resistor_2_node[29]));
  Pull_Resistor pull_resistor_8 (.node(pull_resistor_2_node[30]));
  Pull_Resistor pull_resistor_9 (.node(pull_resistor_2_node[31]));
  or or_1 (ALU_ENABLE, and_1_out, and_2_out);
  and and_1 (and_1_out, IR_INPUT[4], IR_INPUT[3]);
  Pull_Resistor pull_resistor_10 (.node(pull_resistor_10_node[31]));
  Multiplexer #(.width(3)) multiplexer_2 (
    .in0(IR_INPUT[2:0]), .in1(pull_resistor_11_node), .out(multiplexer_2_out), .sel(and_1_out));
  Pull_Resistor pull_resistor_11 (.node(pull_resistor_11_node));
  assign ALU_OP_OUT = IR_INPUT[2:0] | multiplexer_2_out;  // OR_Gate or_2, 3 bits wide
  Pull_Resistor #(.pull(1)) pull_resistor_12 (.node(pull_resistor_12_node));
  Demultiplexer #(.select(5)) demultiplexer_1 (.in(pull_resistor_12_node));  // open: out0, out1, out2, out3, out4, out5, out6, out7, out8, out9, out10, out11, out12, out13, out14, out15, out16, out17, out18, out19, out20, out21, out22, out23, out24, out25, out26, out27, out28, out29, out30, out31, sel
  not not_1 (not_1_out, IR_INPUT[3]);
  and and_2 (and_2_out, IR_INPUT[4], not_1_out);
  Multiplexer #(.width(32)) multiplexer_3 (
    .in0({{8{pull_resistor_10_node[31]}}, IR_INPUT[31:8]}), .in1(multiplexer_5_out), .out(ALU_OPERAND_OUT),
    .sel(and_1_out));
  Multiplexer #(.width(3)) multiplexer_4 (
    .in0(multiplexer_2_out), .in1(pull_resistor_13_node), .out(multiplexer_4_out), .sel(and_2_out));
  Pull_Resistor pull_resistor_13 (.node(pull_resistor_13_node));
  Multiplexer #(.select(3), .width(32)) multiplexer_5 (
    .in0(G4_IN), .in1(G3_IN), .in2(G2_IN), .in3(G1_IN), .in4(FLAG_IN), .in5(AUX_IN), .in6(PC_IN),
    .in7(ACC_IN), .out(multiplexer_5_out), .sel(IR_INPUT[7:5]));
  Multiplexer #(.select(3), .width(32)) multiplexer_6 (
    .in0(G4_IN), .in1(G3_IN), .in2(G2_IN), .in3(G1_IN), .in4(FLAG_IN), .in5(AUX_IN), .in6(PC_IN),
    .in7(ACC_IN), .out(multiplexer_6_out), .sel({IR_INPUT[8], IR_INPUT[9], IR_INPUT[10]}));
  not not_2 (not_2_out, IR_INPUT[4]);
  and and_3 (and_3_out, not_2_out, IR_INPUT[3]);
  not not_3 (not_3_out, multiplexer_4_out[0]);
  and and_4 (and_4_out, and_3_out, and_6_out);
  not not_4 (not_4_out, multiplexer_4_out[2]);
  not not_5 (not_5_out, multiplexer_4_out[1]);
  and and_5 (and_5_out, not_4_out, not_5_out);
  not not_6 (not_6_out, multiplexer_4_out[0]);
  and and_6 (and_6_out, not_3_out, and_5_out);
  and and_7 (and_7_out, and_5_out, multiplexer_4_out[0]);
  and and_8 (and_8_out, and_3_out, and_11_out);
  and and_9 (and_9_out, and_3_out, and_7_out);
  or or_3 (or_3_out, and_9_out, and_4_out);
  Multiplexer #(.width(3)) multiplexer_7 (
    .in0(multiplexer_4_out), .in1(pull_resistor_14_node), .out(multiplexer_7_out), .sel(and_3_out));
  Pull_Resistor pull_resistor_14 (.node(pull_resistor_14_node));
  not not_7 (not_7_out, multiplexer_4_out[2]);
  and and_10 (and_10_out, not_7_out, multiplexer_4_out[1]);
  not not_8 (not_8_out, multiplexer_4_out[0]);
  and and_11 (and_11_out, not_6_out, and_10_out);
  and and_12 (and_12_out, and_10_out, multiplexer_4_out[0]);
  and and_13 (and_13_out, and_3_out, and_12_out);
  and and_14 (and_14_out, and_3_out, and_16_out);
  or or_4 (PC_WRITE_ENABLE, or_3_out, demultiplexer_2_out6);
  Demultiplexer #(.select(3)) demultiplexer_2 (
    .out0(G4_WRITE_ENABLE), .out1(G3_WRITE_ENABLE), .out2(G2_WRITE_ENABLE), .out3(G1_WRITE_ENABLE),
    .out4(FLAG_WRITE_ENABLE), .out5(AUX_WRITE_ENABLE), .out6(demultiplexer_2_out6), .out7(ACC_WRITE_ENABLE),
    .in(and_4_out), .sel(IR_INPUT[7:5]));
  not not_9 (not_9_out, multiplexer_4_out[1]);
  and and_15 (and_15_out, multiplexer_4_out[2], not_9_out);
  not not_10 (not_10_out, multiplexer_4_out[0]);
  and and_16 (and_16_out, not_8_out, and_15_out);
  and and_17 (and_17_out, and_15_out, multiplexer_4_out[0]);
  and and_18 (and_18_out, not_10_out, and_21_out);
  and and_19 (and_19_out, and_3_out, and_17_out);
  and and_20 (and_20_out, and_3_out, and_18_out);
  and and_21 (and_21_out, multiplexer_4_out[2], multiplexer_4_out[1]);
  and and_22 (and_22_out, and_21_out, multiplexer_4_out[0]);
  and and_23 (and_23_out, and_3_out, and_22_out);
  not not_11 (not_11_out, IR_INPUT[4]);
  not not_12 (not_12_out, IR_INPUT[3]);
  and and_24 (and_24_out, not_11_out, not_12_out);
  not not_13 (not_13_out, multiplexer_7_out[0]);
  and and_25 (and_25_out, and_24_out, and_27_out);
  not not_14 (not_14_out, multiplexer_7_out[2]);
  not not_15 (not_15_out, multiplexer_7_out[1]);
  and and_26 (and_26_out, not_14_out, not_15_out);
  and and_27 (and_27_out, not_13_out, and_26_out);
  and and_28 (and_28_out, and_26_out, multiplexer_7_out[0]);
  not not_16 (not_16_out, multiplexer_7_out[0]);
  and and_29 (and_29_out, and_24_out, and_28_out);
  and and_30 (and_30_out, and_24_out, and_32_out);
  not not_17 (not_17_out, multiplexer_7_out[2]);
  and and_31 (and_31_out, not_17_out, multiplexer_7_out[1]);
  not not_18 (not_18_out, multiplexer_7_out[0]);
  and and_32 (and_32_out, not_16_out, and_31_out);
  and and_33 (and_33_out, and_31_out, multiplexer_7_out[0]);
  and and_34 (and_34_out, and_24_out, and_33_out);
  and and_35 (and_35_out, and_24_out, and_37_out);
  not not_19 (not_19_out, multiplexer_7_out[1]);
  and and_36 (and_36_out, multiplexer_7_out[2], not_19_out);
  not not_20 (not_20_out, multiplexer_7_out[0]);
  and and_37 (and_37_out, not_18_out, and_36_out);
  and and_38 (and_38_out, and_36_out, multiplexer_7_out[0]);
  and and_39 (and_39_out, not_20_out, and_42_out);
  and and_40 (and_40_out, and_24_out, and_38_out);
  and and_41 (and_41_out, and_24_out, and_39_out);
  and and_42 (and_42_out, multiplexer_7_out[2], multiplexer_7_out[1]);
  and and_43 (and_43_out, and_42_out, multiplexer_7_out[0]);
  and and_44 (and_44_out, and_24_out, and_43_out);
  Multiplexer #(.width(32)) multiplexer_8 (
    .in0(multiplexer_5_out), .in1({pull_resistor_2_node, multiplexer_1_out}), .out(PC_OUT), .sel(and_4_out));

  assign MEM_ADDR_OUT = IR_INPUT[31:8];

  // Notes on the sheet:
  //   Reg Arithmetic
  //   11
  //   10
  //   reg operand 2
  //   Immediate Arithmetic
  //   reg operand 1
  //   reg operand 2
  //   01
  //   000
  //   1
  //   Data manip/branching
  //   10
  //   01
  //   11
  //   00
  //   0
  //   000
  //   1
  //   Data manip/branching
  //   10
  //   01
  //   11
endmodule

module ALU (
  input  [2:0] OPCODE_SELECTOR,
  input  [31:0] ACC,
  input  [31:0] OPERAND_REG,
  output [31:0] ACC_OUT,
  output [31:0] CR_OUT,
  output [31:0] FLAGS_OUT
);

  wire add_32_1_output_1, and_1_out, and_2_out, and_3_out, and_4_out, and_5_out, and_6_out, and_7_out,
       and_8_out, and_9_out, and_10_out, and_11_out, and_12_out, and_13_out, not_1_out, not_2_out, not_3_out,
       not_4_out, not_5_out, not_6_out, or_2_out, or_3_out;
  wire [1:0] or_5_out;
  wire [31:0] add_32_1_output_bus_1, and_32_1_acc_out, demultiplexer_1_out0, demultiplexer_1_out1,
       demultiplexer_2_out0, demultiplexer_2_out1, demultiplexer_3_out0, demultiplexer_3_out1,
       demultiplexer_4_out0, demultiplexer_4_out1, demultiplexer_5_out0, demultiplexer_5_out1,
       demultiplexer_6_out0, demultiplexer_6_out1, demultiplexer_7_out0, demultiplexer_7_out1,
       demultiplexer_8_out0, demultiplexer_8_out1, demultiplexer_9_out0, demultiplexer_9_out1, divider_1_out,
       divider_1_rem, multiplexer_1_out, multiplexer_2_out, multiplexer_3_out, multiplier_1_cout,
       multiplier_1_out, not_32_1_acc_out, or_32_1_out_3, xor_32_1_out_3;

  Demultiplexer #(.width(32)) demultiplexer_1 (
    .out0(demultiplexer_1_out0), .out1(demultiplexer_1_out1), .in(ACC), .sel(and_1_out));
  Demultiplexer #(.width(32)) demultiplexer_2 (
    .out0(demultiplexer_2_out0), .out1(demultiplexer_2_out1), .in(OPERAND_REG), .sel(and_1_out));
  not not_1 (not_1_out, OPCODE_SELECTOR[2]);
  not not_2 (not_2_out, OPCODE_SELECTOR[1]);
  and and_1 (and_1_out, not_1_out, not_2_out);
  and and_2 (and_2_out, and_1_out, OPCODE_SELECTOR[0]);
  buf and_3 (and_3_out, and_4_out);  // AND_Gate
  Demultiplexer #(.width(32)) demultiplexer_3 (
    .out0(demultiplexer_3_out0), .out1(demultiplexer_3_out1), .in(demultiplexer_1_out0), .sel(and_3_out));
  Demultiplexer #(.width(32)) demultiplexer_4 (
    .out0(demultiplexer_4_out0), .out1(demultiplexer_4_out1), .in(demultiplexer_2_out0), .sel(and_3_out));
  not not_3 (not_3_out, OPCODE_SELECTOR[2]);
  and and_4 (and_4_out, not_3_out, OPCODE_SELECTOR[1]);
  and and_5 (and_5_out, and_4_out, OPCODE_SELECTOR[0]);
  Demultiplexer #(.width(32)) demultiplexer_5 (
    .out0(demultiplexer_5_out0), .out1(demultiplexer_5_out1), .in(demultiplexer_3_out1), .sel(and_5_out));
  Demultiplexer #(.width(32)) demultiplexer_6 (
    .out0(demultiplexer_6_out0), .out1(demultiplexer_6_out1), .in(demultiplexer_4_out1), .sel(and_5_out));
  ADD_32 add_32_1 (
    .Control_Pin_72d4b5d9(and_2_out), .Input_bus_2(demultiplexer_2_out1), .Input_bus_1(demultiplexer_1_out1),
    .Output_bus_1(add_32_1_output_bus_1), .Output_1(add_32_1_output_1));
  and and_6 (and_6_out, OPCODE_SELECTOR[2], not_5_out);
  not not_4 (not_4_out, OPCODE_SELECTOR[0]);
  and and_7 (and_7_out, and_6_out, not_4_out);
  buf and_8 (and_8_out, and_7_out);  // AND_Gate
  assign CR_OUT = multiplier_1_cout | divider_1_rem;  // OR_Gate or_1, 32 bits wide
  or or_2 (or_2_out, CR_OUT[31], CR_OUT[30], CR_OUT[29], CR_OUT[28], CR_OUT[27], CR_OUT[26], CR_OUT[25], CR_OUT[24], CR_OUT[23], CR_OUT[22], CR_OUT[21], CR_OUT[20], CR_OUT[19], CR_OUT[18], CR_OUT[17], CR_OUT[16], CR_OUT[15], CR_OUT[14], CR_OUT[13], CR_OUT[12], CR_OUT[11], CR_OUT[10], CR_OUT[9], CR_OUT[8], CR_OUT[7], CR_OUT[6], CR_OUT[5], CR_OUT[4], CR_OUT[3], CR_OUT[2], CR_OUT[1], CR_OUT[0]);
  not not_5 (not_5_out, OPCODE_SELECTOR[1]);
  and and_9 (and_9_out, and_6_out, OPCODE_SELECTOR[0]);
  buf and_10 (and_10_out, and_9_out);  // AND_Gate
  Multiplier #(.width(32)) multiplier_1 (
    .a(demultiplexer_5_out0), .b(demultiplexer_6_out0), .out(multiplier_1_out), .cout(multiplier_1_cout));  // open: cin
  Divider #(.width(32)) divider_1 (
    .a(demultiplexer_5_out1), .b(demultiplexer_6_out1), .out(divider_1_out), .rem(divider_1_rem));  // open: upper
  and and_11 (and_11_out, OPCODE_SELECTOR[2], OPCODE_SELECTOR[1]);
  and and_12 (and_12_out, and_11_out, not_6_out);
  Multiplexer #(.width(32)) multiplexer_1 (
    .in0(multiplier_1_out), .in1(divider_1_out), .out(multiplexer_1_out), .sel(and_5_out));
  Demultiplexer #(.width(32)) demultiplexer_7 (
    .out0(demultiplexer_7_out0), .out1(demultiplexer_7_out1), .in(demultiplexer_3_out0), .sel(and_8_out));
  Demultiplexer #(.width(32)) demultiplexer_8 (
    .out0(demultiplexer_8_out0), .out1(demultiplexer_8_out1), .in(demultiplexer_4_out0), .sel(and_10_out));
  not not_6 (not_6_out, OPCODE_SELECTOR[0]);
  and and_13 (and_13_out, and_11_out, OPCODE_SELECTOR[0]);
  or or_3 (or_3_out, and_8_out, and_10_out);
  Demultiplexer #(.width(32)) demultiplexer_9 (
    .out0(demultiplexer_9_out0), .out1(demultiplexer_9_out1), .in(demultiplexer_3_out0), .sel(and_12_out));
  OR_32 or_32_1 (.in_1(demultiplexer_7_out1), .in_2(demultiplexer_8_out0), .out_3(or_32_1_out_3));
  AND_32 and_32_1 (.Input_bus_1(demultiplexer_7_out0), .Input_bus_2(demultiplexer_8_out1), .ACC_OUT(and_32_1_acc_out));
  Multiplexer #(.width(32)) multiplexer_2 (
    .in0(or_32_1_out_3), .in1(and_32_1_acc_out), .out(multiplexer_2_out), .sel(and_10_out));
  or or_4 (FLAGS_OUT[0], or_2_out, add_32_1_output_1);
  NOT_32 not_32_1 (.ACC_IN(demultiplexer_9_out1), .ACC_OUT(not_32_1_acc_out));
  XOR_32 xor_32_1 (.in_1(demultiplexer_9_out0), .in_2(demultiplexer_4_out0), .out_3(xor_32_1_out_3));
  Multiplexer #(.width(32)) multiplexer_3 (
    .in0(not_32_1_acc_out), .in1(xor_32_1_out_3), .out(multiplexer_3_out), .sel(and_13_out));
  or or_5 (or_5_out[0], or_3_out, and_1_out);
  or or_6 (or_5_out[1], and_3_out, and_1_out);
  Multiplexer #(.select(2), .width(32)) multiplexer_4 (
    .in0(multiplexer_3_out), .in1(multiplexer_2_out), .in2(multiplexer_1_out), .in3(add_32_1_output_bus_1),
    .out(ACC_OUT), .sel(or_5_out));

  // Notes on the sheet:
  //   On = Sub
  //   Off = Add
  //   On = DIV
  //   Off = MULT
  //   or_1 drives only 1 and floats otherwise
endmodule

module NOT_32 (
  input  [31:0] ACC_IN,
  output [31:0] ACC_OUT
);

  not not_1 (ACC_OUT[0], ACC_IN[0]);
  not not_2 (ACC_OUT[1], ACC_IN[1]);
  not not_3 (ACC_OUT[2], ACC_IN[2]);
  not not_4 (ACC_OUT[3], ACC_IN[3]);
  not not_5 (ACC_OUT[4], ACC_IN[4]);
  not not_6 (ACC_OUT[5], ACC_IN[5]);
  not not_7 (ACC_OUT[6], ACC_IN[6]);
  not not_8 (ACC_OUT[7], ACC_IN[7]);
  not not_9 (ACC_OUT[8], ACC_IN[8]);
  not not_10 (ACC_OUT[9], ACC_IN[9]);
  not not_11 (ACC_OUT[10], ACC_IN[10]);
  not not_12 (ACC_OUT[11], ACC_IN[11]);
  not not_13 (ACC_OUT[12], ACC_IN[12]);
  not not_14 (ACC_OUT[13], ACC_IN[13]);
  not not_15 (ACC_OUT[14], ACC_IN[14]);
  not not_16 (ACC_OUT[15], ACC_IN[15]);
  not not_17 (ACC_OUT[16], ACC_IN[16]);
  not not_18 (ACC_OUT[17], ACC_IN[17]);
  not not_19 (ACC_OUT[18], ACC_IN[18]);
  not not_20 (ACC_OUT[19], ACC_IN[19]);
  not not_21 (ACC_OUT[20], ACC_IN[20]);
  not not_22 (ACC_OUT[21], ACC_IN[21]);
  not not_23 (ACC_OUT[22], ACC_IN[22]);
  not not_24 (ACC_OUT[23], ACC_IN[23]);
  not not_25 (ACC_OUT[24], ACC_IN[24]);
  not not_26 (ACC_OUT[25], ACC_IN[25]);
  not not_27 (ACC_OUT[26], ACC_IN[26]);
  not not_28 (ACC_OUT[27], ACC_IN[27]);
  not not_29 (ACC_OUT[28], ACC_IN[28]);
  not not_30 (ACC_OUT[29], ACC_IN[29]);
  not not_31 (ACC_OUT[30], ACC_IN[30]);
  not not_32 (ACC_OUT[31], ACC_IN[31]);
endmodule
